# Fritzing sketch Light sensor (saved by Fritzing 0.9.5d)
breadboards: 1

parts:
  Компонент1 = Arduino Nano (Rev3.0) (ICSP)
  Компонент2 = LCD1602-I2C
  Mod1 = KY-018 Photoresistor Module [package="Breakout board"]

nets:
  GND: Компонент1.GND, Компонент2.GND, Mod1.-
  5V: Компонент1.5V, Компонент2.VCC, Mod1.Vin
  N1: Компонент1.A5, Компонент2.SCL
  N2: Компонент1.A4, Компонент2.SDA
  N3: Компонент1.A0, Mod1.S

custom parts:
  LCD1602-I2C: A standard character display, usually with 2x16 characters. Comes in many colors with LCM1602 IIC attached.
  KY-018 Photoresistor Module: KY-018 Photoresistor module, used to measure light intensity. It can determine the presence or absence of light.
