# Fritzing sketch Potentiometer (saved by Fritzing 0.9.5d)
breadboards: 1

parts:
  Компонент1 = Arduino Nano (Rev3.0) (ICSP)
  Компонент2 = LCD1602-I2C
  R2 = Rotary Potentiometer (Small) [maximum_resistance=100kΩ package=THT]

nets:
  GND: Компонент1.GND, Компонент2.GND, R2.leg2
  5V: Компонент1.5V, Компонент2.VCC, R2.leg1
  N1: Компонент1.A5, Компонент2.SCL
  N2: Компонент1.A4, Компонент2.SDA
  N3: Компонент1.A0, R2.wiper

custom parts:
  LCD1602-I2C: A standard character display, usually with 2x16 characters. Comes in many colors with LCM1602 IIC attached.
