# Fritzing sketch Rain sensor (saved by Fritzing 0.9.5d)
breadboards: 1

parts:
  Компонент1 = Arduino Nano (Rev3.0) (ICSP)
  Компонент2 = LCD1602-I2C
  부품3 = FC-28 Soil Hygrometer Module
  YL-83_-_Detection_Board2 = YL-83 Rain Sensor - Detection Board

nets:
  GND: Компонент1.GND, Компонент2.GND
  5V: Компонент1.5V, Компонент2.VCC
  N1: Компонент1.A5, Компонент2.SCL
  N2: Компонент1.A4, Компонент2.SDA
  N3: 부품3.POS, YL-83_-_Detection_Board2.POS
  N4: 부품3.NEG, YL-83_-_Detection_Board2.NEG

custom parts:
  LCD1602-I2C: A standard character display, usually with 2x16 characters. Comes in many colors with LCM1602 IIC attached.
  FC-28 Soil Hygrometer Module: The FC-28 is a soil hygrometer module that uses the Texas Instruments LM393 comparator chip to provide an analog measurement of soil humidity. The digital output is high when soil moisture is over a certain threshold, as determined by adjusting the potentiometer.
  YL-83 Rain Sensor - Detection Board: The YL-83 is a rain sensor that has more resistance when dry and less resistance when wet. The module runs at 5V.
