# Fritzing sketch Water level sensor (saved by Fritzing 0.9.5d)
breadboards: 1

parts:
  Компонент1 = Arduino Nano (Rev3.0) (ICSP)
  Компонент2 = LCD1602-I2C
  Water_Level_Sensor1 = Water Level Sensor

nets:
  GND: Компонент1.GND, Компонент2.GND, Water_Level_Sensor1.GND
  VCC: Компонент1.5V, Компонент2.VCC, Water_Level_Sensor1.VCC
  N1: Компонент1.A5, Компонент2.SCL
  N2: Компонент1.A4, Компонент2.SDA
  N3: Компонент1.A0, Water_Level_Sensor1.SIG

custom parts:
  LCD1602-I2C: A standard character display, usually with 2x16 characters. Comes in many colors with LCM1602 IIC attached.
  Water Level Sensor: A water level sensor. This sensor operates at 3V to 5V. The Sig (signal) pin outputs an analogue signal that is in proportion to the amount of water in contact with the sensor.
