# Fritzing sketch One TX (saved by Fritzing 0.9.5d)
breadboards: 1

parts:
  S1 = Pushbutton [package="[THT]"]
  U1 = FS1000A [package=THT]
  Компонент4 = Arduino Uno (Rev3) - ICSP
  LED1 = LED - 3mm [color="Blue (470nm)" package="3 mm [THT]"]
  R1 = Resistor [tolerance=±5% resistance=220 package=THT]

nets:
  N1: S1.Pin_1, S1.Pin_2
  N2: S1.Pin_3, S1.Pin_4, Компонент4.A0
  N3: U1.DATA, Компонент4.5V
  N4: U1.VCC, Компонент4.D4
  GND: U1.GND, Компонент4.GND, LED1.cathode
  N5: Компонент4.D12/MISO, R1.Pin_0
  N6: LED1.anode, R1.Pin_1

custom parts:
  FS1000A: This is 433Mhz RF transmitter with receiver kit for Arduino ARM MCU wireless Application environment: Remote control switch, receiver module, motorcycles, automobile anti-theft products, home security products, electric doors, shutter doors, windows, remote control socket, remote control LED, remote audio remote control electric doors, garage door remote control, remote control retractable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
