# Fritzing sketch Two RX (saved by Fritzing 0.9.5d)
breadboards: 1

parts:
  Компонент1 = Arduino Nano (Rev3.0)
  U1 = XD-RF-5V [package=THT]
  LED1 = LED - 3mm [color="Blue (470nm)" package="3 mm [THT]"]
  R1 = Resistor [tolerance=±5% resistance=220 package=THT]

nets:
  GND: Компонент1.GND, Компонент1.D9, U1.GND, R1.Pin_1
  N1: Компонент1.D2, U1.DATA#2
  N2: Компонент1.D12/MISO, LED1.anode
  5V: Компонент1.5V, U1.VCC
  N3: LED1.cathode, R1.Pin_0

custom parts:
  XD-RF-5V: This is 433Mhz RF transmitter with receiver kit for Arduino ARM MCU wireless Application environment: Remote control switch, receiver module, motorcycles, automobile anti-theft products, home security products, electric doors, shutter doors, windows, remote control socket, remote control LED, remote audio remote control electric doors, garage door remote control, remote control retractable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
