# Fritzing sketch Three RX (saved by Fritzing 0.9.5d)
breadboards: 1

parts:
  Компонент1 = Arduino Nano (Rev3.0)
  U1 = XD-RF-5V [package=THT]
  LED1 = LED - 3mm [color="Blue (470nm)" package="3 mm [THT]"]
  R1 = Resistor [tolerance=±5% resistance=220 package=THT]
  Компонент2 = LCD1602-I2C

nets:
  GND: Компонент1.GND, Компонент1.D9, U1.GND, R1.Pin_1, Компонент2.GND
  N1: Компонент1.D2, U1.DATA#2
  N2: Компонент1.D12/MISO, LED1.anode
  VCC: Компонент1.5V, U1.VCC, Компонент2.VCC
  N3: Компонент1.A5, Компонент2.SCL
  N4: Компонент1.A4, Компонент2.SDA
  N5: LED1.cathode, R1.Pin_0

custom parts:
  XD-RF-5V: This is 433Mhz RF transmitter with receiver kit for Arduino ARM MCU wireless Application environment: Remote control switch, receiver module, motorcycles, automobile anti-theft products, home security products, electric doors, shutter doors, windows, remote control socket, remote control LED, remote audio remote control electric doors, garage door remote control, remote control retractable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
  LCD1602-I2C: A standard character display, usually with 2x16 characters. Comes in many colors with LCM1602 IIC attached.
