# Fritzing sketch Three TX (saved by Fritzing 0.9.5d)
breadboards: 2

parts:
  U1 = FS1000A [package=THT]
  Компонент4 = Arduino Uno (Rev3) - ICSP
  LED1 = LED - 3mm [color="Blue (470nm)" package="3 mm [THT]"]
  R1 = Resistor [tolerance=±5% resistance=220 package=THT]
  Mod1 = KY-015 Temperature & Humidity Sensor Module [package="Breakout board"]

nets:
  N1: U1.DATA, Компонент4.5V
  N2: U1.VCC, Компонент4.D4
  GND: U1.GND, Компонент4.GND, LED1.cathode
  N3: Компонент4.D8, Mod1.S
  N4: Компонент4.D12/MISO, R1.Pin_0
  N5: LED1.anode, R1.Pin_1

custom parts:
  FS1000A: This is 433Mhz RF transmitter with receiver kit for Arduino ARM MCU wireless Application environment: Remote control switch, receiver module, motorcycles, automobile anti-theft products, home security products, electric doors, shutter doors, windows, remote control socket, remote control LED, remote audio remote control electric doors, garage door remote control, remote control retractable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
  KY-015 Temperature & Humidity Sensor Module: KY-015 temperature and humidity sensor module, provides a low-latency serial interface to measure humidity and temperature.
